// Logisim project MIPS.circ as structural Verilog: 5 circuits, main circuit main
module main (
  input  Clear,
  output [7:0] ReadData1,
  output [7:0] out_3,
  output [7:0] ReadData2,
  output [7:0] WriteData
);

  wire and_1_out, and_2_out, CLK_out, control_unit_1_alusrca, control_unit_1_branchequal,
       control_unit_1_branchnotequal, control_unit_1_jump, control_unit_1_memread, control_unit_1_memtoreg,
       control_unit_1_memwrite, control_unit_1_regdst, control_unit_1_regwrite,
       mips_alu_8_bit_by_tushar_2_p4, not_1_out, not_2_out, not_3_out, or_1_out;
  wire [1:0] control_unit_1_alusrcb;
  wire [2:0] control_unit_1_aluop;
  wire [3:0] multiplexer_1_out;
  wire [7:0] bit_extender_1_out, data_memory_1_readdata, mips_alu_8_bit_by_tushar_1_p4,
       mips_alu_8_bit_by_tushar_2_p5, mips_alu_8_bit_by_tushar_3_p4, multiplexer_2_out, multiplexer_3_out,
       multiplexer_4_out, register_1_q, rom_1_data_2;
  wire [19:8] rom_1_data;

  Clock CLK (.out(CLK_out));
  Register #(.trigger("falling")) register_1 (.D(out_3), .Q(register_1_q), .clk(CLK_out), .clr(Clear));  // open: en
  // MIPS_ALU_8_bit_by_Tushar mips_alu_8_bit_by_tushar_1: pin names not known; wires that end beside it: register_1_q, 8'h1, 3'b000, mips_alu_8_bit_by_tushar_1_p4
  ROM #(.dataWidth(20)) rom_1 (.addr(register_1_q), .data({rom_1_data, rom_1_data_2}));  // open: sel
  assign bit_extender_1_out = {{4{1'b0}}, rom_1_data_2[3:0]};  // Bit_Extender bit_extender_1
  Multiplexer #(.width(4), .enable("false")) multiplexer_1 (
    .in0(rom_1_data[11:8]), .in1(rom_1_data_2[7:4]), .out(multiplexer_1_out), .sel(control_unit_1_regdst));
  Control_Unit control_unit_1 (
    .Opcode(rom_1_data[19:16]), .RegWrite(control_unit_1_regwrite), .ALUSrcA(control_unit_1_alusrca),
    .MemWrite(control_unit_1_memwrite), .ALUOp(control_unit_1_aluop), .MemtoReg(control_unit_1_memtoreg),
    .MemRead(control_unit_1_memread), .BranchEqual(control_unit_1_branchequal), .Jump(control_unit_1_jump),
    .RegDst(control_unit_1_regdst), .BranchNotEqual(control_unit_1_branchnotequal),
    .ALUSrcB(control_unit_1_alusrcb));
  Register_file register_file_1 (
    .ReadRegister1(rom_1_data[15:12]), .ReadRegister2(rom_1_data[11:8]), .ReadData1(ReadData1),
    .ReadData2(ReadData2), .WriteData(WriteData), .WriteRegister(multiplexer_1_out),
    .RegWrite(control_unit_1_regwrite), .CLK(not_1_out), .Reset(Clear));
  not not_1 (not_1_out, CLK_out);
  Multiplexer #(.width(8), .enable("false")) multiplexer_2 (
    .in0(ReadData1), .in1(bit_extender_1_out), .out(multiplexer_2_out), .sel(control_unit_1_alusrca));
  Multiplexer #(.select(2), .width(8), .enable("false")) multiplexer_3 (
    .in0(ReadData2), .in1(rom_1_data_2), .in2(ReadData1), .in3({8{1'b0}}), .out(multiplexer_3_out),
    .sel(control_unit_1_alusrcb));
  // MIPS_ALU_8_bit_by_Tushar mips_alu_8_bit_by_tushar_2: pin names not known; wires that end beside it: multiplexer_2_out, multiplexer_3_out, control_unit_1_aluop, mips_alu_8_bit_by_tushar_2_p4, mips_alu_8_bit_by_tushar_2_p5
  // MIPS_ALU_8_bit_by_Tushar mips_alu_8_bit_by_tushar_3: pin names not known; wires that end beside it: mips_alu_8_bit_by_tushar_1_p4, rom_1_data_2, 3'b000, mips_alu_8_bit_by_tushar_3_p4
  not not_2 (not_2_out, mips_alu_8_bit_by_tushar_2_p4);
  and and_1 (and_1_out, control_unit_1_branchnotequal, not_2_out);
  or or_1 (or_1_out, and_1_out, and_2_out);
  and and_2 (and_2_out, control_unit_1_branchequal, mips_alu_8_bit_by_tushar_2_p4);
  Data_Memory data_memory_1 (
    .Address(mips_alu_8_bit_by_tushar_2_p5), .WriteData(ReadData2), .MemRead(control_unit_1_memread),
    .MemWrite(control_unit_1_memwrite), .ReadData(data_memory_1_readdata), .CLK(not_3_out), .Reset(Clear));
  not not_3 (not_3_out, CLK_out);
  Multiplexer #(.width(8), .enable("false")) multiplexer_4 (
    .in0(mips_alu_8_bit_by_tushar_1_p4), .in1(mips_alu_8_bit_by_tushar_3_p4), .out(multiplexer_4_out),
    .sel(or_1_out));
  Multiplexer #(.width(8), .enable("false")) multiplexer_5 (
    .in0(mips_alu_8_bit_by_tushar_2_p5), .in1(data_memory_1_readdata), .out(WriteData),
    .sel(control_unit_1_memtoreg));
  Multiplexer #(.width(8), .enable("false")) multiplexer_6 (
    .in0(multiplexer_4_out), .in1(rom_1_data[15:8]), .out(out_3), .sel(control_unit_1_jump));

  // Notes on the sheet:
  //   PC
  //   Instruction Memory
  //   contents of rom_1 (hex, n*v repeats v):
  //   d07ff d0105 e1240 71401 41900 1052 a5420 c2150 85420 32200 b2114 92103 22203 62021 41800 97200 57701
  //   97100 57701 27200 d7701 27100 d7701 41900 f21f6
endmodule

module _8_bit_ALU (
  input  [7:0] Operand_A,
  input  [7:0] Operand_B,
  input  [2:0] Operation,
  output Zero,
  output [7:0] Result,
  output Overflow
);

  // MIPS_ALU_8_bit_by_Tushar mips_alu_8_bit_by_tushar_1: pin names not known; wires that end beside it: Operand_A, Operand_B, Operation, Zero, Result, Overflow
endmodule

module Register_file (
  input  [3:0] ReadRegister1,
  input  [3:0] ReadRegister2,
  input  [7:0] WriteData,
  input  RegWrite,
  input  [3:0] WriteRegister,
  input  CLK,
  input  Reset,
  output [7:0] ReadData1,
  output [7:0] ReadData2
);

  wire demultiplexer_1_out0, demultiplexer_1_out1, demultiplexer_1_out2, demultiplexer_1_out3,
       demultiplexer_1_out4, demultiplexer_1_out5, demultiplexer_1_out6, demultiplexer_1_out7;
  wire [7:0] multiplexer_3_out, sp_q, t0_q, t1_q, t2_q, t3_q, t4_q, t5_q, zero_q;

  Demultiplexer #(.select(3), .enable("false")) demultiplexer_1 (
    .out0(demultiplexer_1_out0), .out1(demultiplexer_1_out1), .out2(demultiplexer_1_out2),
    .out3(demultiplexer_1_out3), .out4(demultiplexer_1_out4), .out5(demultiplexer_1_out5),
    .out6(demultiplexer_1_out6), .out7(demultiplexer_1_out7), .in(RegWrite), .sel(WriteRegister[2:0]));
  Register #(.trigger("falling")) zero (.D({8{1'b0}}), .en(demultiplexer_1_out0), .Q(zero_q), .clk(CLK), .clr(Reset));
  Register #(.trigger("falling")) t0 (.D(WriteData), .en(demultiplexer_1_out1), .Q(t0_q), .clk(CLK), .clr(Reset));
  Register #(.trigger("falling")) t1 (.D(WriteData), .en(demultiplexer_1_out2), .Q(t1_q), .clk(CLK), .clr(Reset));
  Register #(.trigger("falling")) t2 (.D(WriteData), .en(demultiplexer_1_out3), .Q(t2_q), .clk(CLK), .clr(Reset));
  Register #(.trigger("falling")) t3 (.D(WriteData), .en(demultiplexer_1_out4), .Q(t3_q), .clk(CLK), .clr(Reset));
  Register #(.trigger("falling")) t4 (.D(WriteData), .en(demultiplexer_1_out5), .Q(t4_q), .clk(CLK), .clr(Reset));
  Register #(.trigger("falling")) t5 (.D(WriteData), .en(demultiplexer_1_out6), .Q(t5_q), .clk(CLK), .clr(Reset));
  Multiplexer #(.select(3), .width(8), .enable("false")) multiplexer_1 (
    .in0(zero_q), .in1(t0_q), .in2(t1_q), .in3(t2_q), .in4(t3_q), .in5(t4_q), .in6(t5_q), .in7(sp_q),
    .out(ReadData1), .sel(ReadRegister1[2:0]));
  Multiplexer #(.select(3), .width(8), .enable("false")) multiplexer_2 (
    .in0(zero_q), .in1(t0_q), .in2(t1_q), .in3(t2_q), .in4(t3_q), .in5(t4_q), .in6(t5_q), .in7(sp_q),
    .out(ReadData2), .sel(ReadRegister2[2:0]));
  Register #(.trigger("falling")) sp (
    .D(multiplexer_3_out), .en(demultiplexer_1_out7), .Q(sp_q), .clk(CLK));  // open: clr
  Multiplexer #(.width(8), .enable("false")) multiplexer_3 (
    .in0(WriteData), .in1({8{1'b1}}), .out(multiplexer_3_out), .sel(Reset));
endmodule

module Control_Unit (
  input  [3:0] Opcode,
  output RegWrite,
  output ALUSrcA,
  output MemWrite,
  output [2:0] ALUOp,
  output MemtoReg,
  output MemRead,
  output BranchEqual,
  output Jump,
  output RegDst,
  output BranchNotEqual,
  output [1:0] ALUSrcB
);

  wire [15:14] rom_1_data;

  ROM #(.addrWidth(4), .dataWidth(16)) rom_1 (
    .addr(Opcode),
    .data({rom_1_data, ALUSrcB, BranchNotEqual, RegDst, Jump, BranchEqual, MemRead, MemtoReg, ALUOp, MemWrite, ALUSrcA, RegWrite}));  // open: sel

  // Notes on the sheet:
  //   contents of rom_1 (hex, n*v repeats v):
  //   242b 419 10c1 1019 200 1009 2433 108 421 1004 409 1011 411 1001 401 908
endmodule

module Data_Memory (
  input  [7:0] Address,
  input  [7:0] WriteData,
  input  MemRead,
  input  MemWrite,
  input  CLK,
  input  Reset,
  output [7:0] ReadData
);

  wire and_1_out;

  and and_1 (and_1_out, MemWrite, CLK);
  RAM #(.bus("separate")) ram_1 (
    .addr(Address), .din(WriteData), .data(ReadData), .str(MemWrite), .clk(and_1_out), .ld(MemRead),
    .clr(Reset));  // open: sel
endmodule
